# Fritzing sketch digital graffiti (saved by Fritzing 1.0.6)
circuit board: 3.72703cm x 4.71104cm
breadboards: 1

parts:
  R1 = Resistor [tolerance=±5% resistance=220 package="0603 [SMD]"]
  R2 = Resistor [tolerance=±5% resistance=220 package="0603 [SMD]"]
  R3 = Basic Force Sensing Resistor (FSR) [package=THT]
  Battery = Battery block 9V [internal_resistance=0.1Ω]
  U1 = Arduino Nano (Rev3.0)
  LED1 = RGB LED (com. cathode, rgb) [color="Red (633nm)" current=30mA package="5 mm [THT]"]
  R4 = Resistor [tolerance=±5% resistance=220 package="0603 [SMD]"]

nets (from the schematic view):
  N1: R1.Pin_0, LED1.green_anode
  N2: R1.Pin_1, U1.D10
  N3: R2.Pin_0, LED1.blue_anode
  N4: R2.Pin_1, U1.D11/MOSI
  N5: R3.pin_1, U1.3V3
  N6: R3.pin_2, U1.A0, R4.Pin_0
  N7: Battery.-, U1.GND, LED1.common_cathode, R4.Pin_1
  N8: Battery.+, U1.VIN

// code stored in the sketch: digital graffiti.ino
void setup() {
	analogWrite(10, 128);
	analogWrite(11, 255);
}

void loop() {}
