# Fritzing sketch meds tracker (saved by Fritzing 1.0.6)
breadboards: 1

parts:
  LED5 = 7-SEGMENT-4DIGIT-YOUNGSUN [package=7-segment-4digit-youngsun]
  U3 = 74HC595 SMD [package="SO16 [SMD]"]
  R12 = Resistor [tolerance=±5% resistance=560 package="0402 [SMD]"]
  R11 = Resistor [tolerance=±5% resistance=560 package="0402 [SMD]"]
  R10 = Resistor [tolerance=±5% resistance=560 package="0402 [SMD]"]
  R9 = Resistor [tolerance=±5% resistance=560 package="0402 [SMD]"]
  R6 = Resistor [tolerance=±5% resistance=560 package="0402 [SMD]"]
  R7 = Resistor [tolerance=±5% resistance=560 package="0402 [SMD]"]
  R8 = Resistor [tolerance=±5% resistance=560 package="0402 [SMD]"]
  LED6 = 7-SEGMENT-4DIGIT-YOUNGSUN [package=7-segment-4digit-youngsun]
  LED2 = smd LED [color="Red (633nm)" current=0A package="1206 [SMD]"]
  LED1 = smd LED [color="Green (555nm)" package="1206 [SMD]"]
  R2 = Rotary Potentiometer (Small) [maximum_resistance=100kΩ knob_status=50% power=0.5W package=THT]
  LED4 = smd LED [color="Red (633nm)" package="1206 [SMD]"]
  LED3 = smd LED [color="Green (555nm)" package="1206 [SMD]"]
  R1 = Rotary Potentiometer (Small) [maximum_resistance=100kΩ knob_status=50% power=0.5W package=THT]
  R4 = Resistor [tolerance=±5% resistance=560 package="0402 [SMD]"]
  R3 = Resistor [tolerance=±5% resistance=560 package="0402 [SMD]"]
  R5 = Resistor [tolerance=±5% resistance=560 package="0402 [SMD]"]
  R6_2 = Resistor [tolerance=±5% resistance=560 package="0402 [SMD]"]
  U2 = 74HC595 SMD [package="SO16 [SMD]"]
  U1 = Arduino Uno (Rev3) - ICSP
  US2 = HC-SR04 Ultrasonic Distance Sensor
  US1 = HC-SR04 Ultrasonic Distance Sensor

nets:
  N1: LED5.DIG1, U2.Q0
  N2: LED5.DIG2, U2.Q1
  N3: LED5.D, R9.Pin_1, LED6.D
  N4: LED5.E, R10.Pin_1, LED6.E
  N5: LED5.DIG3, U2.Q2
  N6: LED5.DIG4, U2.Q3
  N7: LED5.F, R11.Pin_1, LED6.F
  N8: LED5.C, R8.Pin_1, LED6.C
  N9: LED5.A, R6.Pin_1, LED6.A
  N10: LED5.G, R12.Pin_1, LED6.G
  N11: LED5.B, R7.Pin_1, LED6.B
  N12: U3.Q1, R6.Pin_0
  N13: U3.Q2, R7.Pin_0
  N14: U3.Q3, R8.Pin_0
  N15: U3.Q4, R9.Pin_0
  N16: U3.Q5, R10.Pin_0
  N17: U3.Q6, R11.Pin_0
  N18: U3.Q7, R12.Pin_0
  GND: U3.GND, LED2.cathode, LED1.cathode, R2.leg1, LED4.cathode, LED3.cathode, R1.leg1, U2.GND, U2.OE, U1.GND, US2.GND, US1.GND
  VCC: U3.MR, U3.VCC, R2.leg2, R1.leg2, U2.MR, U2.VCC, U1.5V, US2.VCC, US1.VCC
  N19: U3.SH_CP, U3.ST_CP, U1.D3_PWM
  N20: U3.OE, U1.D2
  N21: U3.DS, U1.D1/TX
  N22: LED6.DIG1, U2.Q4
  N23: LED6.DIG2, U2.Q5
  N24: LED6.DIG3, U2.Q6
  N25: LED6.DIG4, U2.Q7
  N26: LED2.anode, R4.Pin_1
  N27: LED1.anode, R3.Pin_1
  N28: R2.wiper, U1.A1
  N29: LED4.anode, R6_2.Pin_1
  N30: LED3.anode, R5.Pin_1
  N31: R1.wiper, U1.A0
  N32: R4.Pin_0, U1.D8
  N33: R3.Pin_0, U1.D7
  N34: R5.Pin_0, U1.D12/MISO
  N35: R6_2.Pin_0, U1.D13/SCK
  N36: U2.SH_CP, U2.ST_CP, U1.D5_PWM
  N37: U2.DS, U1.D4
  N38: U1.ICSP_MOSI, U1.D11_PWM/MOSI, US2.TRIG
  N39: U1.D9_PWM, US1.TRIG
  N40: U1.D10_PWM/SS, US2.ECHO
  N41: U1.D6_PWM, US1.ECHO
