# Fritzing sketch salt-shaker-sturdy (saved by Fritzing 1.0.6)
stripboards: 2
breadboards: 1

parts:
  Part2 = Arduino Uno (Rev3) - ICSP  # not connected
  Part4 = Triple Axis Accelerometer Breakout - ADXL345
  SG3 = Buzzer 12mm [part_number=COM-07950 package=buzzer-12mm-ns]

nets:
  N1: Part4.GND, Part4.CS, SG3.1

custom parts:
  Buzzer 12mm: Buzzer 12mm Spark Fun Electronics SKU : Comp-Buzzer Through hole This is a small 12mm round speaker that operates around the audible 2kHz range. You can use these speakers to create simple music or user interfaces. This is not a true piezoelectric speaker but behaves similarly. Instead of a piezoelectric crystal that vibrates with an electric current, this tiny speaker uses an electromagnet to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
